# Fritzing sketch HalfAdder Fritzing Project (saved by Fritzing 0.9.3b)
breadboards: 1

parts:
  R1 = Resistor [tolerance=±5% resistance=10k package="2512 [SMD]"]
  S2 = Pushbutton [package=THT]
  R2 = Resistor [tolerance=±5% resistance=10k package=THT]
  S3 = Pushbutton [package=THT]
  IC1 = 74HC08 Logic AND Gate [part_number=74HC08 package="DIP (Dual Inline) [THT]"]
  R3 = Resistor [tolerance=±5% resistance=330 package=THT]
  LED1 = LED - 3mm [color="Red (633nm)" package="3 mm [THT]"]
  LED2 = LED - 3mm [color="Red (633nm)" package="3 mm [THT]"]
  R4 = Resistor [tolerance=±5% resistance=330 package=THT]
  IC2 = 4070 4 x 2 Input XOR Gate, single part [part_number=74HC86 package="DIP (Dual Inline) [THT]"]

nets:
  GND: R1.Pin_0, R2.Pin_0, IC1.GND, R3.Pin_0, R4.Pin_0, IC2.GND
  N1: R1.Pin_1, S2.leg0, IC1.3A, IC2.B3
  VCC: S2.leg1, S3.leg1, IC1.VCC, IC2.VDD
  N2: R2.Pin_1, S3.leg0, IC1.3B, IC2.Q3
  N3: IC1.3Y, LED2.anode
  N4: R3.Pin_1, LED1.cathode
  N5: LED1.anode, IC2.A3
  N6: LED2.cathode, R4.Pin_1

notes:
  +5 v
  GND
  S
  C
  a
  b

custom parts:
  4070 4 x 2 Input XOR Gate, single part: 4070 4 x 2 Input XOR Gate as a single part
